# Fritzing sketch R.Hasika_perfboard (saved by Fritzing 0.9.2b)
perfboards: 1

parts:
  Composant1 = Arduino Nano (Rev3.0)
  U1 = Voltage Regulator - 5V [package="TO220 [THT]"]
  VCC1 = Battery
  S2 = Pushbutton [package="[THT]"]
  S3 = Pushbutton [package="[THT]"]
  J2 = Infrared Proximity Sensor
  S4 = Toggle Switch [package=THT]  # not connected
  S5 = Toggle Switch [package=THT]
  R1 = Resistor [tolerance=±5% resistance=1k package=THT]
  R2 = Resistor [tolerance=±5% resistance=1k package=THT]
  Raspberry_Pi1 = Raspberry Pi B+

nets:
  N1: Composant1.D1/TX, R1.Pin_1
  GND: Composant1.GND, U1.GND, S2.Pin_1, S2.Pin_2, S3.Pin_1, S3.Pin_2, J2.GND, R2.Pin_1
  N2: Composant1.D4, S3.Pin_3, S3.Pin_4
  N3: Composant1.D5, S2.Pin_3, S2.Pin_4
  5V: Composant1.5V, J2.Vcc, S5.L2, Raspberry_Pi1.5V
  N4: Composant1.A0, J2.Vout
  N5: U1.input_voltage, VCC1.+
  N6: U1.output_voltage, S5.COM
  N7: VCC1.-, Raspberry_Pi1.GND
  N8: R1.Pin_0, R2.Pin_0, Raspberry_Pi1.GPIO15

notes:
  leftContactSwith
  rightContactSwith
  RasPi RX
  RasPi TX
